# Fritzing sketch schematic (saved by Fritzing 1.0.4)
breadboards: 1

parts:
  A1 = Particle - Photon2
  MOTOR1 = 28BYJ-48 Stepper Motor
  X1 = X113647 Stepper Driver Board [part_number=X113647 package=board]
  X2 = X113647 Stepper Driver Board [part_number=X113647 package=board]
  MOTOR2 = 28BYJ-48 Stepper Motor
  Q1 = TIP120 Hi-Current Darlington Transistor
  LD1 = LD
  Part1 = Thumb Joystick
  OLED_I2C1 = OLED 128x64 I2C Monochrome Display
  Part2 = Adafruit VL530X Time of Flight Distance Sensor [part_number="Adafruit #3317"]

nets:
  VCC: A1.Pin_2, A1.Pin_31, LD1.anode, Part1.VCC, OLED_I2C1.VDD, Part2.VCC
  GND: A1.Pin_4, A1.Pin_30, A1.Pin_33, X1.GND, X2.GND, Q1.BASE, Part1.GND
  N1: A1.Pin_5, Part1.VERT
  N2: A1.Pin_6, Part1.HORZ
  N3: A1.Pin_10, Q1.EMITTER, LD1.cathode
  N4: A1.Pin_11, X1.IN4
  N5: A1.Pin_12, X1.IN3
  N6: A1.Pin_13, X1.IN2
  N7: A1.Pin_14, X1.IN1
  N8: A1.Pin_17, OLED_I2C1.SDA, Part2.SDA
  N9: A1.Pin_18, OLED_I2C1.SCK, Part2.SCL
  N10: A1.Pin_21, X2.IN4
  N11: A1.Pin_22, X2.IN3
  N12: A1.Pin_23, A1.Pin_37, X2.IN2
  N13: A1.Pin_24, A1.Pin_36, X2.IN1
  N14: A1.Pin_25, Part1.SEL
  N15: A1.Pin_26, X1.+V, X2.+V
  N16: MOTOR1.BLUE, X2.BLUE
  N17: MOTOR1.PINK, X2.PINK
  N18: MOTOR1.RED, X2.YELLOW
  N19: MOTOR1.ORANGE, X2.ORANGE
  N20: MOTOR1.YELLOW, X2.RED
  N21: X1.BLUE, MOTOR2.BLUE
  N22: X1.PINK, MOTOR2.PINK
  N23: X1.YELLOW, MOTOR2.RED
  N24: X1.ORANGE, MOTOR2.ORANGE
  N25: X1.RED, MOTOR2.YELLOW
  GND_2: OLED_I2C1.GND, Part2.GND

custom parts:
  Particle - Photon2: The Photon 2 is a microcontroller and Wi-Fi networking developed by particle. Features: 802.11a/b/g/n Wi-Fi, 2.4 GHz and 5 GHz Integrated PCB antenna Integrated U.FL connector for external antenna Integrated RF switch BLE 5 using same antenna as Wi-Fi Realtek RTL8721DM MCU ARM Cortex M33 CPU, 200 MHz 2048 KB (2 MB) user application maximum size 3072 KB (3 MB) of RAM available to user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
  28BYJ-48 Stepper Motor: 28BYJ-48 gear-reduction stepper motor (small)
  X113647 Stepper Driver Board: A common stepper motor driver board based on ULN2003APG darlington array
  LD: A Generic Red Dot Laser Diode Module (~5mW)
  Adafruit VL530X Time of Flight Distance Sensor: The VL53L0X is a Time of Flight distance sensor like no other you've used! The sensor contains a very tiny invisible laser source, and a matching sensor. The VL53L0X can detect the "time of flight", or how long the light has taken to bounce back to the sensor. Since it uses a very narrow light source, it is good for determining distance of only the surface directly in front of it. Unlike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
